# Fritzing sketch MCP3008_Breadboard_Hookup (saved by Fritzing 0.9.3b)
breadboards: 1

parts:
  Part1 = Adafruit T-Cobbler Plus [part_number="Adafruit #1989 and #2028"]
  IC1 = MCP3008 8-channel 10-bit ADC [part_number=MCP3008]
  Raspberry_Pi_1 = Raspberry Pi 3 [part_number=RPI-3-V1.2]

nets:
  3V3: Part1.+3.3V, Part1.+3.3V_2, IC1.no_name_yet#15, IC1.no_name_yet#16, Raspberry_Pi_1.3v3, Raspberry_Pi_1.3V3
  N1: Part1.GPIO19, IC1.no_name_yet#12, Raspberry_Pi_1.GIPO19
  GND: Part1.GND, IC1.no_name_yet#9, IC1.no_name_yet#14, Raspberry_Pi_1.GND
  N2: Part1.GPIO18, IC1.no_name_yet#10, Raspberry_Pi_1.GIPO18
  N3: Part1.GPIO20, IC1.no_name_yet#11, Raspberry_Pi_1.GIPO20
  N4: Part1.GPIO21, IC1.no_name_yet#13, Raspberry_Pi_1.GIPO21
  +5V: Part1.+5V, Raspberry_Pi_1.5V
  N5: Part1.SDA, Raspberry_Pi_1.GPIO2
  N6: Part1.SCL, Raspberry_Pi_1.GPIO3
  N7: Part1.GPIO4, Raspberry_Pi_1.GIPO4
  N8: Part1.TXD, Raspberry_Pi_1.GIPO14
  N9: Part1.RXD, Raspberry_Pi_1.GIPO15
  N10: Part1.GPIO17, Raspberry_Pi_1.GIPO17
  N11: Part1.GPIO27, Raspberry_Pi_1.GIPO27
  N12: Part1.GPIO22, Raspberry_Pi_1.GIPO22
  N13: Part1.GPIO23, Raspberry_Pi_1.GIPO23
  N14: Part1.GPIO24, Raspberry_Pi_1.GIPO24
  N15: Part1.MOSI, Raspberry_Pi_1.GIPO10
  N16: Part1.MISO, Raspberry_Pi_1.GIPO9
  N17: Part1.GPIO25, Raspberry_Pi_1.GIPO25
  N18: Part1.SCLK, Raspberry_Pi_1.GIPO11
  N19: Part1.CE0, Raspberry_Pi_1.GIPO8
  N20: Part1.CE1, Raspberry_Pi_1.GIPO7
  N21: Part1.EEDAT, Raspberry_Pi_1.ID_SD
  N22: Part1.EECLK, Raspberry_Pi_1.ID_SC
  N23: Part1.GPIO5, Raspberry_Pi_1.GIPO5
  N24: Part1.GPIO6, Raspberry_Pi_1.GIPO6
  N25: Part1.GPIO12, Raspberry_Pi_1.GIPO12
  N26: Part1.GPIO13, Raspberry_Pi_1.GIPO13
  N27: Part1.GPIO16, Raspberry_Pi_1.GIPO16
  N28: Part1.GPIO26, Raspberry_Pi_1.GIPO26

custom parts:
  Adafruit T-Cobbler Plus: The Raspberry Pi has landed on the Maker World like a 40-GPIO pinned, quad-USB ported, credit card sized bomb of DIY joy. And while you can use most of our great Model B accessories by hooking up our downgrade cable, its probably a good time to upgrade your set up and accessorize using all of the 40 pins. That's why we now carry the Assembled Adafruit Pi T-Cobbler Plus - Breakout + Cable for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
